# Fritzing sketch schematic (saved by Fritzing 0.8.5b)
stripboards: 1

parts:
  Q3 = Basic FET P-Channel [package="TO220 [THT]"]
  Power_plug1 = Power plug
  Raspberry_Pi_B_rev1 = Raspberry Pi B rev2
  Q4 = Basic FET P-Channel [package="TO220 [THT]"]
  Q5 = Basic FET P-Channel [package="TO220 [THT]"]
  LED1 = RGB LED (com. cathode, rgb) [package="5 mm [THT]"]

nets:
  N1: Q3.gate, Raspberry_Pi_B_rev1.GPIO_24
  N2: Q3.drain, LED1.common_cathode
  GND: Q3.source, Power_plug1.GND, Raspberry_Pi_B_rev1.GND, Q4.source, Q5.source
  N3: Power_plug1.VCC, LED1.blue_anode
  N4: Raspberry_Pi_B_rev1.GPIO_23, Q4.gate
  N5: Raspberry_Pi_B_rev1.GPIO_18, Q5.gate
  N6: Q4.drain, LED1.green_anode
  N7: Q5.drain, LED1.red_anode

custom parts:
  RGB LED (com. cathode, rgb): A 5mm tri-color LED with red, green and blue inside.
